// Logisim project alu.circ as structural Verilog: 2 circuits, main circuit alu
module alu (
  input  [31:0] A,
  input  [31:0] B,
  input  [3:0] ALUSel,
  output [31:0] Result
);

  wire comparator_1_lt;
  wire [4:0] bit_extender_1_out, bit_extender_2_out, bit_extender_3_out;
  wire [31:0] add, and1, bit_extender_5_out, bit_extender_6_out, divu1, mul1, mulh1, mulhu1,
       multiplier_2_cout, multiplier_3_out, multiplier_4_out, or1, remu1, sll1, slt1, sra1, srl1, sub1,
       vaddrh1, xor1;

  assign or1 = A | B;  // OR_Gate or_1, 32 bits wide
  assign xor1 = A ^ B;  // XOR_Gate xor_1, 32 bits wide
  Shifter #(.width(32), .shift("lr")) shifter_1 (.in(A), .\dist (bit_extender_1_out), .out(srl1));
  Bit_Extender #(.in_width(32), .out_width(5), .\type ("zero")) bit_extender_1 (.in(B), .out(bit_extender_1_out));
  Shifter #(.width(32), .shift("ar")) shifter_2 (.in(A), .\dist (bit_extender_2_out), .out(sra1));
  Bit_Extender #(.in_width(32), .out_width(5), .\type ("zero")) bit_extender_2 (.in(B), .out(bit_extender_2_out));
  Shifter #(.width(32)) shifter_3 (.in(A), .\dist (bit_extender_3_out), .out(sll1));
  Bit_Extender #(.in_width(32), .out_width(5), .\type ("zero")) bit_extender_3 (.in(B), .out(bit_extender_3_out));
  Comparator #(.width(32)) comparator_1 (.a(A), .b(B), .lt(comparator_1_lt));  // open: gt, eq
  andcir andcir_1 (.A(A), .B(B), .outt(and1));
  assign slt1 = {{31{1'b0}}, comparator_1_lt};  // Bit_Extender bit_extender_4
  Divider #(.width(32)) divider_1 (.a(A), .b(B), .out(divu1), .rem(remu1));  // open: upper
  Multiplier #(.width(32)) multiplier_1 (.a(A), .b(B), .out(mul1), .cin({32{1'b0}}), .cout(mulhu1));
  Subtractor #(.width(32)) subtractor_1 (.a(A), .b(B), .out(sub1));  // open: bin, bout
  Multiplier #(.width(32)) multiplier_2 (.a(A), .b(B), .cin({32{1'b0}}), .cout(multiplier_2_cout));  // open: out
  assign bit_extender_5_out = {{31{A[31]}}, A[31]};  // Bit_Extender bit_extender_5
  assign bit_extender_6_out = {{31{B[31]}}, B[31]};  // Bit_Extender bit_extender_6
  Adder #(.width(32)) adder_1 (.a(A), .b(B), .out(add));  // open: cin, cout
  Adder #(.width(16)) adder_2 (.a(A[15:0]), .b(B[15:0]), .out(vaddrh1[15:0]));  // open: cin, cout
  Adder #(.width(16)) adder_3 (.a(A[31:16]), .b(B[31:16]), .out(vaddrh1[31:16]));  // open: cin, cout
  Multiplier #(.width(32)) multiplier_3 (
    .a(bit_extender_5_out), .b(B), .out(multiplier_3_out), .cin(multiplier_2_cout));  // open: cout
  Multiplier #(.width(32)) multiplier_4 (.a(bit_extender_6_out), .b(A), .out(multiplier_4_out));  // open: cin, cout
  Adder #(.width(32)) adder_4 (.a(multiplier_3_out), .b(multiplier_4_out), .out(mulh1));  // open: cin, cout
  Multiplexer #(.select(4), .width(32), .enable("false")) multiplexer_1 (
    .in0(add), .in1(and1), .in2(or1), .in3(xor1), .in4(srl1), .in5(sra1), .in6(sll1), .in7(slt1),
    .in8(divu1), .in9(remu1), .in10(mul1), .in11(mulhu1), .in12(sub1), .in13(B), .in14(mulh1),
    .in15(vaddrh1), .out(Result), .sel(ALUSel));

  // Other names for the same wires on the sheet: bsel1[31:0] = B

  // Notes on the sheet:
  //   INPUTS to your circuit
  //   DON'T CHANGE THE LOCATIONS OF THE INPUTS AND OUTPUTS!
  //   OUTPUT from your circuit
endmodule

module andcir (
  input  [31:0] A,
  input  [31:0] B,
  output [31:0] outt
);

  assign outt = A & B;  // AND_Gate and_1, 32 bits wide
endmodule
