// Logisim project cpu.circ as structural Verilog: 4 circuits, main circuit main
module main (
  input  [31:0] INSTRUCTION,
  input  CLOCK,
  output [31:0] FETCH_ADDRESS,
  output [31:0] ra,
  output [31:0] sp,
  output [31:0] t0,
  output [31:0] t1,
  output [31:0] t2,
  output [31:0] s0,
  output [31:0] s1,
  output [31:0] a0
);

  wire BREQ, BRLT, BRUN, control_1_asel, control_1_bsel, control_1_memrw, control_1_regwen, PC_SEL;
  wire [1:0] control_1_wbsel;
  wire [2:0] control_1_immsel, multiplexer_5_out;
  wire [3:0] control_1_alusel;
  wire [7:0] multiplexer_7_out;
  wire [15:0] multiplexer_6_out;
  wire [31:0] ALUOUT, bit_extender_1_out, bit_extender_2_out, DMEM_p5, EXECPC, EXECPCPLUS4, immgen_1_imm,
       main_1_read_data_1, main_1_read_data_2, multiplexer_1_out, multiplexer_2_out, multiplexer_3_out,
       multiplexer_4_out, multiplexer_8_out, PCPLUS4, TOEXEC, WD;

  Adder #(.width(32)) adder_1 (.a(FETCH_ADDRESS), .b(32'h4), .out(PCPLUS4));  // open: cin, cout
  Multiplexer #(.width(32), .enable("false")) multiplexer_1 (
    .in0(PCPLUS4), .in1(ALUOUT), .out(multiplexer_1_out), .sel(PC_SEL));
  Register #(.width(32)) register_1 (.D(FETCH_ADDRESS), .clk(CLOCK), .Q(EXECPC));  // open: en, clr
  Multiplexer #(.width(32), .enable("false")) multiplexer_2 (
    .in0(INSTRUCTION), .in1(32'h13), .out(multiplexer_2_out), .sel(PC_SEL));
  Register #(.width(32)) PC (.D(multiplexer_1_out), .clk(CLOCK), .Q(FETCH_ADDRESS));  // open: en, clr
  Register #(.width(32)) register_2 (.D(multiplexer_2_out), .clk(CLOCK), .Q(TOEXEC));  // open: en, clr
  Adder #(.width(32)) adder_2 (.a(EXECPC), .b(32'h4), .out(EXECPCPLUS4));  // open: cin, cout
  Control control_1 (
    .ASel(control_1_asel), .Instruction(TOEXEC), .BSel(control_1_bsel), .BrEq(BREQ), .BrUn(BRUN),
    .BrLt(BRLT), .ImmSel(control_1_immsel), .PCSel(PC_SEL), .RegWEn(control_1_regwen),
    .ALUSel(control_1_alusel), .MemRW(control_1_memrw), .WBSel(control_1_wbsel));
  regfile_main main_1 (
    .rs2(TOEXEC[24:20]), .rd(TOEXEC[11:7]), .Read_Data_1(main_1_read_data_1),
    .Read_Data_2(main_1_read_data_2), .ra(ra), .sp(sp), .t0(t0), .t1(t1), .t2(t2), .s0(s0), .s1(s1), .a0(a0),
    .rs1(TOEXEC[19:15]), .Write_Data(WD), .RegWEn(control_1_regwen), .clk(CLOCK));
  ImmGen immgen_1 (.Inst31to7(TOEXEC), .ImmSel(control_1_immsel), .imm(immgen_1_imm));
  Multiplexer #(.width(32), .enable("false")) multiplexer_3 (
    .in0(main_1_read_data_1), .in1(EXECPC), .out(multiplexer_3_out), .sel(control_1_asel));
  Multiplexer #(.width(32), .enable("false")) multiplexer_4 (
    .in0(main_1_read_data_2), .in1(immgen_1_imm), .out(multiplexer_4_out), .sel(control_1_bsel));
  Branch branch_1 (.rs1(main_1_read_data_1), .rs2(main_1_read_data_2), .BrUn(BRUN), .BrEq(BREQ), .BrLt(BRLT));
  alu alu_1 (.A(multiplexer_3_out), .B(multiplexer_4_out), .ALUSel(control_1_alusel), .Result(ALUOUT));
  // mem_main DMEM: pin names not known; wires that end beside it: ALUOUT, main_1_read_data_2, control_1_memrw, CLOCK, DMEM_p5
  Multiplexer #(.width(3), .enable("false")) multiplexer_5 (
    .in0(3'b000), .in1(TOEXEC[14:12]), .out(multiplexer_5_out), .sel(control_1_wbsel[1]));
  assign bit_extender_1_out = {{16{multiplexer_6_out[15]}}, multiplexer_6_out};  // Bit_Extender bit_extender_1
  Multiplexer #(.width(16), .enable("false")) multiplexer_6 (
    .in0(DMEM_p5[15:0]), .in1(DMEM_p5[31:16]), .out(multiplexer_6_out), .sel(ALUOUT[1]));
  Multiplexer #(.select(2), .width(8), .enable("false")) multiplexer_7 (
    .in0(DMEM_p5[7:0]), .in1(DMEM_p5[15:8]), .in2(DMEM_p5[23:16]), .in3(DMEM_p5[31:24]),
    .out(multiplexer_7_out), .sel(ALUOUT[1:0]));
  assign bit_extender_2_out = {{24{multiplexer_7_out[7]}}, multiplexer_7_out};  // Bit_Extender bit_extender_2
  Multiplexer #(.select(3), .width(32), .enable("false")) multiplexer_8 (
    .in0(bit_extender_2_out), .in1(bit_extender_1_out), .in2(DMEM_p5), .out(multiplexer_8_out),
    .sel(multiplexer_5_out));  // open: in3, in4, in5, in6, in7
  Multiplexer #(.select(2), .width(32), .enable("false")) multiplexer_9 (
    .in0(EXECPCPLUS4), .in1(ALUOUT), .in2(multiplexer_8_out), .out(WD), .sel(control_1_wbsel));  // open: in3

  // Other names for the same wires on the sheet: clk = CLOCK; PROGRAM_COUNTER[31:0] = FETCH_ADDRESS

  // Notes on the sheet:
  //   Output
  //   Inputs/Outputs from run.circ. DO NOT MOVE THESE.
  //   Inputs
  //   Inputs/Outputs from run.circ. DO NOT MOVE THESE.
endmodule

module Control (
  input  [31:0] Instruction,
  input  BrEq,
  input  BrLt,
  output [2:0] ImmSel,
  output BrUn,
  output [1:0] WBSel,
  output PCSel,
  output [3:0] ALUSel,
  output RegWEn,
  output BSel,
  output ASel,
  output MemRW
);

  wire and_1_out, and_7_out, and_9_out, BRANCH, I, JALR, LOAD, multiplexer_2_out, not_1_out, not_2_out,
       not_3_out, not_4_out, not_5_out, not_6_out, not_7_out, not_8_out, not_9_out, not_10_out, not_11_out,
       not_12_out, not_13_out, not_14_out, not_15_out, not_16_out, not_17_out, not_18_out, not_19_out,
       not_20_out, not_21_out, not_22_out, not_23_out, not_24_out, not_25_out, not_26_out, or_1_out,
       or_2_out, or_3_out, or_4_out, or_5_out, or_6_out, or_8_out, R, S, SB, U, UJ;
  wire [1:0] multiplexer_21_out;
  wire [2:0] multiplexer_6_out, multiplexer_7_out, multiplexer_8_out, multiplexer_9_out;
  wire [3:0] multiplexer_14_out, multiplexer_15_out, multiplexer_16_out, multiplexer_17_out,
       multiplexer_19_out, multiplexer_22_out, multiplexer_23_out, multiplexer_24_out, multiplexer_25_out,
       multiplexer_26_out, multiplexer_27_out, multiplexer_28_out;

  and and_1 (and_1_out, BRANCH, SB);
  not not_1 (not_1_out, Instruction[2]);
  not not_2 (not_2_out, Instruction[3]);
  not not_3 (not_3_out, Instruction[6]);
  not not_4 (not_4_out, Instruction[2]);
  not not_5 (not_5_out, Instruction[3]);
  not not_6 (not_6_out, Instruction[4]);
  not not_7 (not_7_out, Instruction[6]);
  or or_1 (or_1_out, R, S, U);
  or or_2 (or_2_out, UJ, JALR, and_1_out);
  or or_3 (or_3_out, R, I, U, UJ);
  or or_4 (or_4_out, I, S, SB, U, UJ);
  and and_2 (R, not_1_out, not_2_out, Instruction[4], Instruction[5], not_3_out);
  and and_3 (S, not_4_out, not_5_out, not_6_out, Instruction[5], not_7_out);
  Multiplexer #(.enable("false")) multiplexer_1 (.in0(multiplexer_2_out), .in1(1'b0), .out(PCSel), .sel(or_1_out));
  Multiplexer #(.enable("false")) multiplexer_2 (.in0(1'b0), .in1(1'b1), .out(multiplexer_2_out), .sel(or_2_out));
  Multiplexer #(.enable("false")) multiplexer_3 (.in0(1'b0), .in1(1'b1), .out(RegWEn), .sel(or_3_out));
  Multiplexer #(.enable("false")) multiplexer_4 (.in0(1'b0), .in1(1'b1), .out(BSel), .sel(or_4_out));
  or or_5 (or_5_out, SB, UJ);
  not not_8 (not_8_out, Instruction[2]);
  not not_9 (not_9_out, Instruction[3]);
  not not_10 (not_10_out, Instruction[4]);
  not not_11 (not_11_out, Instruction[3]);
  not not_12 (not_12_out, Instruction[6]);
  not not_13 (not_13_out, Instruction[4]);
  Multiplexer #(.width(3), .enable("false")) multiplexer_5 (
    .in0(multiplexer_6_out), .in1(3'b000), .out(ImmSel), .sel(I));
  Multiplexer #(.width(3), .enable("false")) multiplexer_6 (
    .in0(multiplexer_7_out), .in1(3'b001), .out(multiplexer_6_out), .sel(S));
  Multiplexer #(.width(3), .enable("false")) multiplexer_7 (
    .in0(multiplexer_8_out), .in1(3'b010), .out(multiplexer_7_out), .sel(SB));
  Multiplexer #(.width(3), .enable("false")) multiplexer_8 (
    .in0(multiplexer_9_out), .in1(3'b011), .out(multiplexer_8_out), .sel(U));
  Multiplexer #(.width(3), .enable("false")) multiplexer_9 (
    .in0(3'b101), .in1(3'b100), .out(multiplexer_9_out), .sel(UJ));
  Multiplexer #(.enable("false")) multiplexer_10 (.in0(1'b0), .in1(1'b1), .out(ASel), .sel(or_5_out));
  and and_4 (SB, not_8_out, not_9_out, not_10_out, Instruction[5], Instruction[6]);
  and and_5 (U, Instruction[2], not_11_out, Instruction[4], Instruction[5], not_12_out);
  and and_6 (UJ, Instruction[2], Instruction[3], not_13_out, Instruction[5], Instruction[6]);
  Multiplexer #(.enable("false")) multiplexer_11 (.in0(1'b0), .in1(1'b1), .out(MemRW), .sel(S));
  and and_7 (and_7_out, SB, Instruction[13]);
  Multiplexer #(.enable("false")) multiplexer_12 (.in0(1'b0), .in1(1'b1), .out(BrUn), .sel(and_7_out));
  Multiplexer #(.select(2), .enable("false")) multiplexer_13 (
    .in0(BrEq), .in1(not_14_out), .in2(BrLt), .in3(not_15_out), .out(BRANCH),
    .sel({Instruction[14], Instruction[12]}));
  not not_14 (not_14_out, BrEq);
  not not_15 (not_15_out, BrLt);
  not not_16 (not_16_out, Instruction[2]);
  not not_17 (not_17_out, Instruction[3]);
  not not_18 (not_18_out, Instruction[4]);
  not not_19 (not_19_out, Instruction[5]);
  not not_20 (not_20_out, Instruction[6]);
  not not_21 (not_21_out, Instruction[2]);
  not not_22 (not_22_out, Instruction[3]);
  not not_23 (not_23_out, Instruction[5]);
  not not_24 (not_24_out, Instruction[6]);
  not not_25 (not_25_out, Instruction[3]);
  not not_26 (not_26_out, Instruction[4]);
  Multiplexer #(.width(4), .enable("false")) multiplexer_14 (
    .in0(4'b0100), .in1(4'b0101), .out(multiplexer_14_out), .sel(Instruction[30]));
  and and_8 (LOAD, Instruction[1], not_16_out, not_17_out, not_18_out, not_19_out, not_20_out);
  and and_9 (and_9_out, not_21_out, not_22_out, Instruction[4], not_23_out, not_24_out);
  and and_10 (JALR, Instruction[2], not_25_out, not_26_out, Instruction[5], Instruction[6]);
  Multiplexer #(.width(4), .enable("false")) multiplexer_15 (
    .in0(4'b0000), .in1(multiplexer_17_out), .out(multiplexer_15_out), .sel(I));
  or or_6 (or_6_out, LOAD, S, SB, UJ, JALR);
  Multiplexer #(.width(4), .enable("false")) multiplexer_16 (
    .in0(multiplexer_15_out), .in1(multiplexer_26_out), .out(multiplexer_16_out), .sel(R));
  Multiplexer #(.select(3), .width(4), .enable("false")) multiplexer_17 (
    .in0(4'b0000), .in1(4'b0110), .in2(4'b0111), .in4(4'b0011), .in5(multiplexer_14_out), .in6(4'b0010),
    .in7(4'b0001), .out(multiplexer_17_out), .sel(Instruction[14:12]));  // open: in3
  or or_7 (I, LOAD, and_9_out, JALR);
  or or_8 (or_8_out, JALR, UJ);
  Multiplexer #(.width(4), .enable("false")) multiplexer_18 (
    .in0(multiplexer_19_out), .in1(4'b0000), .out(ALUSel), .sel(or_6_out));
  Multiplexer #(.width(4), .enable("false")) multiplexer_19 (
    .in0(multiplexer_16_out), .in1(4'b1101), .out(multiplexer_19_out), .sel(U));
  Multiplexer #(.width(2), .enable("false")) multiplexer_20 (
    .in0(multiplexer_21_out), .in1(2'b10), .out(WBSel), .sel(LOAD));
  Multiplexer #(.width(2), .enable("false")) multiplexer_21 (
    .in0(2'b01), .in1(2'b00), .out(multiplexer_21_out), .sel(or_8_out));
  Multiplexer #(.width(4), .enable("false")) multiplexer_22 (
    .in0(4'b0000), .in1(4'b1100), .out(multiplexer_22_out), .sel(Instruction[30]));
  Multiplexer #(.width(4), .enable("false")) multiplexer_23 (
    .in0(4'b1010), .in1(4'b1111), .out(multiplexer_23_out), .sel(Instruction[26]));
  Multiplexer #(.width(4), .enable("false")) multiplexer_24 (
    .in0(multiplexer_22_out), .in1(multiplexer_23_out), .out(multiplexer_24_out), .sel(Instruction[25]));
  Multiplexer #(.width(4), .enable("false")) multiplexer_25 (
    .in0(4'b0100), .in1(4'b1000), .out(multiplexer_25_out), .sel(Instruction[25]));
  Multiplexer #(.select(3), .width(4), .enable("false")) multiplexer_26 (
    .in0(multiplexer_24_out), .in1(multiplexer_28_out), .in2(4'b0111), .in3(4'b1011), .in4(4'b0011),
    .in5(multiplexer_25_out), .in6(4'b0010), .in7(multiplexer_27_out), .out(multiplexer_26_out),
    .sel(Instruction[14:12]));
  Multiplexer #(.width(4), .enable("false")) multiplexer_27 (
    .in0(4'b0001), .in1(4'b1001), .out(multiplexer_27_out), .sel(Instruction[25]));
  Multiplexer #(.width(4), .enable("false")) multiplexer_28 (
    .in0(4'b0110), .in1(4'b1110), .out(multiplexer_28_out), .sel(Instruction[25]));

  // Other names for the same wires on the sheet: FUNCT3[2:0] = Instruction[14:12]; OPCODE[6:0] = Instruction[6:0];
  //   FUNCT7[6:0] = Instruction[31:25]
endmodule

module ImmGen (
  input  [31:0] Inst31to7,
  input  [2:0] ImmSel,
  output [31:0] imm
);

  wire [3:0] L4;
  wire [5:0] L6;
  wire [30:12] I;

  Multiplexer #(.select(3), .width(32), .enable("false")) multiplexer_1 (
    .in0({Inst31to7[31], I, Inst31to7[31:20]}), .in1({Inst31to7[31], I, Inst31to7[31:25], Inst31to7[11:7]}),
    .in2({Inst31to7[31], I, Inst31to7[7], Inst31to7[30:25], Inst31to7[11:8], 1'b0}),
    .in3({Inst31to7[31:12], {12{1'b0}}}),
    .in4({Inst31to7[31], I[30:20], Inst31to7[19:12], Inst31to7[20], Inst31to7[30:21], 1'b0}), .out(imm),
    .sel(ImmSel));  // open: in5, in6, in7
  assign L4 = {{3{Inst31to7[31]}}, Inst31to7[31]};  // Bit_Extender bit_extender_1
  assign L6 = {{5{Inst31to7[31]}}, Inst31to7[31]};  // Bit_Extender bit_extender_2
  assign I[19:12] = {{7{Inst31to7[31]}}, Inst31to7[31]};  // Bit_Extender bit_extender_3
  assign I[30:20] = {{10{Inst31to7[31]}}, Inst31to7[31]};  // Bit_Extender bit_extender_4

  // Other names for the same wires on the sheet: INSTIN[31:0] = Inst31to7;
  //   S[31:0] = {Inst31to7[31], I, Inst31to7[31:25], Inst31to7[11:7]};
  //   SB[31:1] = {Inst31to7[31], I, Inst31to7[7], Inst31to7[30:25], Inst31to7[11:8]}; L8[7:0] = I[19:12];
  //   I (some bits) = {{2{Inst31to7[31]}}, Inst31to7[30:20]}; U[31:12] = Inst31to7[31:12];
  //   UJ[31:1] = {Inst31to7[31], I[30:20], Inst31to7[19:12], Inst31to7[20], Inst31to7[30:21]}; L11[10:0] = I[30:20];
  //   L1 = Inst31to7[31]
endmodule

module Branch (
  input  [31:0] rs1,
  input  [31:0] rs2,
  input  BrUn,
  output BrEq,
  output BrLt
);

  wire comparator_1_lt, comparator_2_lt;

  Comparator #(.width(32)) comparator_1 (.a(rs1), .b(rs2), .eq(BrEq), .lt(comparator_1_lt));  // open: gt
  Comparator #(.width(32), .mode("unsigned")) comparator_2 (.a(rs1), .b(rs2), .lt(comparator_2_lt));  // open: gt, eq
  Multiplexer #(.enable("false")) multiplexer_1 (.in0(comparator_1_lt), .in1(comparator_2_lt), .out(BrLt), .sel(BrUn));
endmodule
